# Fritzing sketch dotmatrix-circuit (saved by Fritzing 0.8.7b)
circuit board: 8.46667cm x 5.64444cm
breadboards: 1

parts:
  U1 = 74HC595 [package="DIP16 [THT]"]
  U2 = 74HC595 [package="DIP16 [THT]"]
  R1 = Resistor [tolerance=±5% resistance=220 package=THT]
  R2 = Resistor [tolerance=±5% resistance=220 package=THT]
  R3 = Resistor [tolerance=±5% resistance=220 package=THT]
  R4 = Resistor [tolerance=±5% resistance=220 package=THT]
  R5 = Resistor [tolerance=±5% resistance=220 package=THT]
  R6 = Resistor [tolerance=±5% resistance=220 package=THT]
  R7 = Resistor [tolerance=±5% resistance=220 package=THT]
  R8 = Resistor [tolerance=±5% resistance=220 package=THT]
  Part1 = Arduino Uno (Rev3)  # not connected

nets:
  N1: U1.Q1, R7.Pin_1
  N2: U1.Q2, R6.Pin_1
  N3: U1.Q3, R1.Pin_1
  N4: U1.Q4, R2.Pin_1
  N5: U1.Q5, R3.Pin_1
  N6: U1.Q6, R4.Pin_1
  N7: U1.Q7, R5.Pin_1
  GND: U1.GND, U1.OE, U2.GND, U2.OE
  N8: U1.Q7', U2.DS
  5V: U1.MR, U1.VCC, U2.MR, U2.VCC
  N9: U1.SH_CP, U2.SH_CP
  N10: U1.ST_CP, U2.ST_CP
  N11: U1.Q0, R8.Pin_1
